# Fritzing sketch esp8266_attiny (saved by Fritzing 0.9.2b)
circuit board: 5cm x 4.8cm
breadboards: 1

parts:
  5VDC_STEPPER = Adafruit Gear-Reduced Stepper Motor (small)
  L293D = L293D [package=THT]
  ESP = ESP8266 WiFi Module [part_number=ESP8266]
  BATT2 = 4xAA Switchable Battery Pack w/JST connector
  LED = LTE-302 [package=lte-302]
  U1 = attiny85 [package=dip]
  FTDI = FTDI Basic Programmer

nets:
  N1: 5VDC_STEPPER.ORANGE, L293D.Out_4_(_Controlled_by_Enable_2_)
  N2: 5VDC_STEPPER.YELLOW, L293D.Out_2_(_Controlled_by_Enable_1_)
  N3: 5VDC_STEPPER.PINK, L293D.Out_3_(_Controlled_by_Enable_2_)
  N4: 5VDC_STEPPER.BLUE, L293D.Out_1_(_Controlled_by_Enable_1_)
  N5: L293D.Enable_1, L293D.+Vmotor, L293D.Enable_2, L293D.+V, ESP.VCC, ESP.CH_PD, BATT2.POS, U1.Pin_8, FTDI.POWER
  N6: L293D.In_1, U1.Pin_5
  GND: L293D.0V, ESP.GND, BATT2.NEG, LED.C, U1.Pin_4, FTDI.GND
  N7: L293D.In_2, U1.Pin_6
  N8: L293D.In_3, U1.Pin_7
  N9: L293D.In_4, U1.Pin_2
  N10: ESP.RXD, FTDI.TXO
  N11: ESP.GPIO_2, LED.A, U1.Pin_3
  N12: ESP.TXD, FTDI.RXI

notes:
  GND
  VCC
  Bad Wolf v4
  VIN
  VOUT
  GND CTS VC TX RX  RT

custom parts:
  Adafruit Gear-Reduced Stepper Motor (small): Adafruit gear-reduction stepper motor (small)
  ESP8266 WiFi Module: Generic WiFi Module based on the ESP8266 with onboard PCB antenna and UART communications
  4xAA Switchable Battery Pack w/JST connector: 4xAA Switchable Battery Pack with JST connector
