# Fritzing sketch esp8266_attiny_noftdi_reg (saved by Fritzing 0.9.2b)
circuit board: 2.62073cm x 2.43972cm
breadboards: 1

parts:
  5VDC_STEPPER = Adafruit Gear-Reduced Stepper Motor (small)
  L293D = L293D [package=THT]
  ATTINY = attiny85 [package=dip]
  B = 4xAA Switchable Battery Pack w/JST connector
  LED = LTE-302 [package=lte-302]
  ESP = ESP8266 WiFi Module [part_number=ESP8266]
  U1 = V_REG_LD1117VXX [package=78xxl]  # not connected
  IC1 = Voltage Regulator [package=78xxl]  # not connected

nets (from the pcb view):
  N1: 5VDC_STEPPER.ORANGE, L293D.Out_4_(_Controlled_by_Enable_2_)
  N2: 5VDC_STEPPER.YELLOW, L293D.Out_2_(_Controlled_by_Enable_1_)
  N3: 5VDC_STEPPER.PINK, L293D.Out_3_(_Controlled_by_Enable_2_)
  N4: 5VDC_STEPPER.BLUE, L293D.Out_1_(_Controlled_by_Enable_1_)
  N5: L293D.Enable_1, L293D.+Vmotor, L293D.Enable_2, L293D.+V, ATTINY.Pin_8, B.POS, ESP.VCC, ESP.CH_PD
  N6: L293D.In_1, ATTINY.Pin_5
  N7: L293D.0V, ATTINY.Pin_4, B.NEG, LED.C, ESP.GND
  N8: L293D.In_2, ATTINY.Pin_6
  N9: L293D.In_3, ATTINY.Pin_7
  N10: L293D.In_4, ATTINY.Pin_2
  N11: ATTINY.Pin_3, LED.A, ESP.GPIO_2

notes:
  badwolf v5

custom parts:
  Adafruit Gear-Reduced Stepper Motor (small): Adafruit gear-reduction stepper motor (small)
  4xAA Switchable Battery Pack w/JST connector: 4xAA Switchable Battery Pack with JST connector
  ESP8266 WiFi Module: Generic WiFi Module based on the ESP8266 with onboard PCB antenna and UART communications
