# Fritzing sketch esp8266_led (saved by Fritzing 0.9.2b)
breadboards: 1

parts:
  U1 = ESP8266 WiFi Module [part_number=ESP8266]
  LED1 = smd LED [color="Red (633nm)" package="1206 [SMD]"]
  BATT1 = LiPoly Battery (1300mAh)

nets:
  N1: U1.VCC, U1.CH_PD, BATT1.positive
  N2: U1.GPIO_2, LED1.anode
  N3: U1.GND, BATT1.negative

custom parts:
  ESP8266 WiFi Module: Generic WiFi Module based on the ESP8266 with onboard PCB antenna and UART communications
  LiPoly Battery (1300mAh): Lithium Ion Polymer Battery (1300mAh)
