# Fritzing sketch esp8266_led_ftdi (saved by Fritzing 0.9.2b)
breadboards: 1

parts:
  U1 = ESP8266 WiFi Module [part_number=ESP8266]
  Part1 = FTDI Basic Programmer
  LED1 = smd LED [color="Red (633nm)" package="1206 [SMD]"]

nets:
  N1: U1.RXD, Part1.TXO
  N2: U1.VCC, U1.CH_PD, Part1.POWER
  GND: U1.GPIO_0, U1.GND, Part1.GND, LED1.cathode
  N3: U1.GPIO_2, LED1.anode
  N4: U1.TXD, Part1.RXI

custom parts:
  ESP8266 WiFi Module: Generic WiFi Module based on the ESP8266 with onboard PCB antenna and UART communications
